# Fritzing sketch mega-wiring (saved by Fritzing 0.9.3b)
breadboards: 1

parts:
  Part1 = Arduino Mega 2560 (Rev3)
  R1 = Resistor [tolerance=±5% resistance=68 power=0.25W package=THT]
  LED1 = LED - 3mm [color="White (6500K)" package="3 mm [THT]"]
  LED2 = LED - 3mm [color="White (6500K)" package="3 mm [THT]"]
  R2 = Resistor [tolerance=±5% resistance=68 power=0.25W package=THT]
  R3 = Resistor [tolerance=±5% resistance=68 power=0.25W package=THT]
  R4 = Resistor [tolerance=±5% resistance=68 power=0.25W package=THT]
  R5 = Resistor [tolerance=±5% resistance=68 power=0.25W package=THT]
  LED3 = LED - 3mm [color="White (6500K)" package="3 mm [THT]"]
  LED4 = LED - 3mm [color="White (6500K)" package="3 mm [THT]"]
  LED5 = LED - 3mm [color="White (6500K)" package="3 mm [THT]"]
  DHT1 = DHT22 Humidity and Temperature Sensor  # not connected
  Part2 = Soil Moisture Sensor
  Part3 = RFID-RC522-v3

nets:
  N1: Part1.A0, Part2.SIG
  5V: Part1.5V, Part2.VCC, Part3.3.3V
  GND: Part1.GND, R1.Pin_0, R2.Pin_0, R3.Pin_0, R4.Pin_0, R5.Pin_0, Part2.GND, Part3.GND
  N2: Part1.D2_PWM, LED5.anode
  N3: Part1.D3_PWM, LED4.anode
  N4: Part1.D4_PWM, LED3.anode
  N5: Part1.D5_PWM, LED2.anode
  N6: Part1.D6_PWM, LED1.anode
  N7: Part1.D49, Part3.RST
  N8: Part1.D50, Part3.MISO
  N9: Part1.D51, Part3.MOSI
  N10: Part1.D52, Part3.SCK
  N11: Part1.D53, Part3.SDA
  N12: R1.Pin_1, LED1.cathode
  N13: LED2.cathode, R2.Pin_1
  N14: R3.Pin_1, LED3.cathode
  N15: R4.Pin_1, LED4.cathode
  N16: R5.Pin_1, LED5.cathode

custom parts:
  RFID-RC522-v3: A simple China made RFID-RC522 Reader (6x4 cm); do check the pin labels, as this is a MFRC522 based clone.
